# Fritzing sketch ESP-201 (saved by Fritzing 0.9.2b)
breadboards: 1

parts:
  U1 = ESP8266 WiFi Module [part_number=ESP8266]
  Part1 = Arduino Uno (Rev3)
  R1 = Resistor [tolerance=±10% resistance=3.3k package=THT]
  R2 = Resistor [tolerance=±10% resistance=1.8k package=THT]
  DHT1 = DHT11 Humitidy and Temperature Sensor
  R3 = Resistor [tolerance=±10% resistance=4.7k package=THT]

nets:
  N1: U1.3.3V#11, U1.CHIP_EN
  N2: U1.GND#12, U1.IO15, R1.Pin_1
  N3: U1.TX, Part1.D10_PWM/SS
  N4: U1.RX, R1.Pin_0, R2.Pin_1
  N5: Part1.D11_PWM/MOSI, R2.Pin_0
  N6: Part1.D2, DHT1.DATA, R3.Pin_1
  5V: Part1.5V, DHT1.VDD, R3.Pin_0
  GND: Part1.GND, DHT1.GND

notes:
  DC 5V to 3.3V
  Step-Down AMS1117
  3.3V

custom parts:
  DHT11 Humitidy and Temperature Sensor: DHT11 Humidity and Temperature Sensor
